# Fritzing sketch kuhomon (saved by Fritzing 0.9.3b)

parts:
  U1 = NodeMCU V1.0
  Part1 = Adafruit_BMP280
  Grove1 = Grove OLED 128x96
  Part2 = Adafruit SHT31-D Sensirion Temperature/Humidity Sensor [part_number="Adafruit #2857"]
  U2 = MH-Z19 CO2 Sensor [chip_label=? package=THT]

nets:
  N1: U1.D1, Part1.SDO/ADR, Grove1.SDA, Part2.SDA
  N2: U1.D2, Part1.SCK/SCL, Grove1.SCL, Part2.SCL
  GND: U1.GND, Part1.GND, Grove1.GND, Part2.GND, U2.GND
  N3: U1.D7, U2.Tx
  N4: U1.D8, U2.Rx
  3V3: U1.3V3, Part1.3.3V, Grove1.VCC, Part2.VIN
  VIN: U1.Vin, U2.Vin

custom parts:
  NodeMCU V1.0: ESP8266 based NodeMCU
  Adafruit_BMP280: Bosch has stepped up their game with their new BMP280 sensor, an environmental sensor with temperature, barometric pressure that is the next generation upgrade to the BMP085/BMP180/BMP183. This sensor is great for all sorts of weather sensing and can even be used in both I2C and SPI! This precision sensor from Bosch is the best low-cost, precision sensing solution for measuring barometric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
  Adafruit SHT31-D Sensirion Temperature/Humidity Sensor: Sensirion Temperature/Humidity sensors are some of the finest & highest-accuracy devices you can get. And, finally we have some that have a true I2C interface for easy reading. The SHT31-D sensor has an excellent ±2% relative humidity and ±0.3°C accuracy for most uses. Unlike earlier SHT sensors, this sensor has a true I2C interface, and (bonus!) even with two address options. It also is 3V or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
